// Logisim project 6502Subset.circ as structural Verilog
module ALU (
  input  [7:0] A,
  input  [7:0] B,
  input  C_IN,
  input  [2:0] ALU_Mux_Control,
  output C_OUT,
  output [7:0] Output,
  output Overflow
);

  wire xnor_1_out, xor_2_out;
  wire [7:0] and_1_out, or_1_out, sr_1_out, sr_b_1_out, sum_1_out, xor_1_out;

  SUM sum_1 (.OUT(sum_1_out), .C_OUT(C_OUT), .A(A), .B(B), .C_IN(C_IN));
  AND and_1 (.A(A), .B(B), .OUT(and_1_out));
  OR or_1 (.A(A), .B(B), .OUT(or_1_out));
  XOR xor_1 (.A(A), .B(B), .OUT(xor_1_out));
  SR sr_1 (.A(A), .OUT(sr_1_out));
  SR_B sr_b_1 (.A(B), .OUT(sr_b_1_out));
  Multiplexer #(.select(3), .width(8)) multiplexer_1 (
    .in0(sum_1_out), .in1(and_1_out), .in2(or_1_out), .in3(xor_1_out), .in4(sr_1_out), .in5(sr_b_1_out),
    .in6(A), .in7(B), .out(Output), .sel(ALU_Mux_Control), .en(1'b1));
  xor xor_2 (xor_2_out, B[7], Output[7]);
  xnor xnor_1 (xnor_1_out, A[7], B[7]);
  and and_2 (Overflow, xnor_1_out, xor_2_out);

  // Notes on the sheet:
  //   ALU
endmodule

module SUM (
  input  C_IN,
  input  [7:0] A,
  input  [7:0] B,
  output [7:0] OUT,
  output C_OUT
);

  Adder adder_1 (.a(A), .b(B), .out(OUT), .cin(C_IN), .cout(C_OUT));

  // Notes on the sheet:
  //   Sum
endmodule

module AND (
  input  [7:0] A,
  input  [7:0] B,
  output [7:0] OUT
);

  assign OUT = A & B;  // AND_Gate and_1, 8 bits wide

  // Notes on the sheet:
  //   And
endmodule

module OR (
  input  [7:0] A,
  input  [7:0] B,
  output [7:0] OUT
);

  assign OUT = A | B;  // OR_Gate or_1, 8 bits wide
endmodule

module XOR (
  input  [7:0] A,
  input  [7:0] B,
  output [7:0] OUT
);

  assign OUT = A ^ B;  // XOR_Gate xor_1, 8 bits wide
endmodule

module SR (
  input  [7:0] A,
  output [7:0] OUT
);

  Shifter #(.shift("lr")) shifter_1 (.in(A), .\dist (3'b001), .out(OUT));
endmodule

module SR_B (
  input  [7:0] A,
  output [7:0] OUT
);

  Shifter #(.shift("lr")) shifter_1 (.in(A), .\dist (3'b001), .out(OUT));
endmodule

module Infrastructure (
  input  [7:0] Input_Data_Latch,
  input  Clock,
  input  IR5,
  input  C_IN,
  input  [31:0] Control_Lines,
  input  [19:0] Control_Lines_2_0,
  output [7:0] ABH,
  output [7:0] ABL,
  output [7:0] OUT
);

  wire [7:0] bus_1_adder_hold_out, bus_1_sb_out, bus_1_sp_out, controlled_buffer_1_out, pc_1_adh_out,
       pc_1_db_out;

  Bus bus_1 (
    .C_IN(C_IN), .ADL_In(controlled_buffer_1_out), .SP_Out(bus_1_sp_out),
    .Adder_Hold_Out(bus_1_adder_hold_out), .Clock(Clock), .SB_Out(bus_1_sb_out), .DB_In(pc_1_db_out),
    .OUT(OUT), .Status_Cntrl_Lines(Control_Lines_2_0[19:16]), .Control_Lines(Control_Lines[30:0]), .IR5(IR5));
  assign controlled_buffer_1_out = Control_Lines_2_0[7] ? bus_1_sp_out : 8'bz;  // Controlled_Buffer controlled_buffer_1
  assign controlled_buffer_1_out = Control_Lines_2_0[8] ? bus_1_adder_hold_out : 8'bz;  // Controlled_Buffer controlled_buffer_2
  PC pc_1 (
    .SB_In(bus_1_sb_out), .in_4({Control_Lines_2_0[15], Control_Lines_2_0[6:0], Control_Lines[31]}),
    .ADL_Out(controlled_buffer_1_out), .ADH_Out(pc_1_adh_out), .ADL_in(controlled_buffer_1_out),
    .DB_Out(pc_1_db_out), .ADH_in(pc_1_adh_out));
  assign pc_1_adh_out = Control_Lines_2_0[9] ? bus_1_sb_out : 8'bz;  // Controlled_Buffer controlled_buffer_3
  assign pc_1_db_out = Control_Lines_2_0[12] ? Input_Data_Latch : 8'bz;  // Controlled_Buffer controlled_buffer_4
  assign ABH = Control_Lines_2_0[10] ? pc_1_adh_out : 8'bz;  // Controlled_Buffer controlled_buffer_5
  assign ABL = Control_Lines_2_0[11] ? controlled_buffer_1_out : 8'bz;  // Controlled_Buffer controlled_buffer_6
  assign controlled_buffer_1_out = Control_Lines_2_0[13] ? Input_Data_Latch : 8'bz;  // Controlled_Buffer controlled_buffer_7
  assign pc_1_adh_out = Control_Lines_2_0[14] ? Input_Data_Latch : 8'bz;  // Controlled_Buffer controlled_buffer_8

  // Other names for the same wires on the sheet: SP_ADL = Control_Lines_2_0[7]; ADD_ADL = Control_Lines_2_0[8];
  //   SB_ADH = Control_Lines_2_0[9]; ADH_ABH = Control_Lines_2_0[10]; ADL_ABL = Control_Lines_2_0[11];
  //   IDL_DB = Control_Lines_2_0[12]; IDL_ADL = Control_Lines_2_0[13]; IDL_ADH = Control_Lines_2_0[14]

  // Notes on the sheet:
  //   Infrastructure
endmodule

module Bus (
  input  Clock,
  input  [30:0] Control_Lines,
  input  [7:0] DB_In,
  input  [3:0] Status_Cntrl_Lines,
  input  IR5,
  input  C_IN,
  input  [7:0] ADL_In,
  output [7:0] OUT,
  output [7:0] SP_Out,
  output [7:0] SB_Out,
  output [7:0] Adder_Hold_Out
);

  wire AVR, COUT, not_1_out, undriven;
  wire [7:0] A_q, ACC_q, alu_1_output, B_q, controlled_buffer_1_out, controlled_buffer_2_out,
       controlled_buffer_3_out, controlled_buffer_11_out, controlled_buffer_13_out, controlled_buffer_14_out,
       X_q, Y_q;

  Register register_1 (.D(DB_In), .Q(OUT), .clk(Control_Lines[19]));  // open: en, clr
  StatusRegister statusregister_1 (
    .DB_In(DB_In), .DB_Out(DB_In), .IR5(IR5), .Control({Status_Cntrl_Lines, Control_Lines[30:20]}),
    .AVR(AVR), .COUT(COUT));
  assign controlled_buffer_1_out = Control_Lines[10] ? DB_In : 8'bz;  // Controlled_Buffer controlled_buffer_1
  Register A (.D(controlled_buffer_1_out), .Q(A_q), .clk(Clock));  // open: en, clr
  Register ACC (.D(controlled_buffer_2_out), .Q(ACC_q), .clk(Clock));  // open: en, clr
  assign controlled_buffer_2_out = Control_Lines[1] ? DB_In : 8'bz;  // Controlled_Buffer controlled_buffer_2
  assign controlled_buffer_3_out = Control_Lines[13] ? DB_In : 8'bz;  // Controlled_Buffer controlled_buffer_3
  Register SP (.D(controlled_buffer_3_out), .Q(SP_Out), .clk(Clock), .clr(undriven));  // open: en
  not not_1 (not_1_out, Clock);
  ALU alu_1 (
    .A(A_q), .B(B_q), .C_IN(C_IN), .Output(alu_1_output), .ALU_Mux_Control(Control_Lines[18:16]),
    .C_OUT(COUT), .Overflow(AVR));
  assign SB_Out = Control_Lines[0] ? ACC_q : 8'bz;  // Controlled_Buffer controlled_buffer_4
  assign DB_In = Control_Lines[2] ? ACC_q : 8'bz;  // Controlled_Buffer controlled_buffer_5
  assign SB_Out = Control_Lines[3] ? SP_Out : 8'bz;  // Controlled_Buffer controlled_buffer_6
  assign DB_In = Control_Lines[4] ? SP_Out : 8'bz;  // Controlled_Buffer controlled_buffer_7
  assign DB_In = Control_Lines[14] ? SB_Out : 8'bz;  // Controlled_Buffer controlled_buffer_8
  Register Adder_Hold (.D(alu_1_output), .Q(Adder_Hold_Out), .clk(not_1_out));  // open: en, clr
  assign SB_Out = Control_Lines[15] ? DB_In : 8'bz;  // Controlled_Buffer controlled_buffer_9
  assign SB_Out = Control_Lines[9] ? Adder_Hold_Out : 8'bz;  // Controlled_Buffer controlled_buffer_10
  Register B (.D(controlled_buffer_11_out), .Q(B_q), .clk(Clock));  // open: en, clr
  assign controlled_buffer_11_out = Control_Lines[11] ? SB_Out : 8'bz;  // Controlled_Buffer controlled_buffer_11
  assign controlled_buffer_11_out = Control_Lines[12] ? ADL_In : 8'bz;  // Controlled_Buffer controlled_buffer_12
  assign controlled_buffer_13_out = Control_Lines[5] ? SB_Out : 8'bz;  // Controlled_Buffer controlled_buffer_13
  assign controlled_buffer_14_out = Control_Lines[7] ? SB_Out : 8'bz;  // Controlled_Buffer controlled_buffer_14
  Register X (.D(controlled_buffer_13_out), .Q(X_q), .clk(Clock));  // open: en, clr
  Register Y (.D(controlled_buffer_14_out), .Q(Y_q), .clk(Clock));  // open: en, clr
  assign SB_Out = Control_Lines[6] ? X_q : 8'bz;  // Controlled_Buffer controlled_buffer_15
  assign SB_Out = Control_Lines[8] ? Y_q : 8'bz;  // Controlled_Buffer controlled_buffer_16

  // Other names for the same wires on the sheet: A_SB = Control_Lines[0]; DB_A = Control_Lines[1];
  //   A_DB = Control_Lines[2]; SP_SB = Control_Lines[3]; SP_DB = Control_Lines[4]; SB_X = Control_Lines[5];
  //   X_SB = Control_Lines[6]; SB_Y = Control_Lines[7]; Y_SB = Control_Lines[8]; Add_SB = Control_Lines[9];
  //   DDB_AA = Control_Lines[10]; SB_AB = Control_Lines[11]; ADL_AB = Control_Lines[12]; DB_SP = Control_Lines[13];
  //   SB_DB = Control_Lines[14]; DB_SB = Control_Lines[15]; OUT_t = Control_Lines[19]

  // Notes on the sheet:
  //   Busses
endmodule

// 1
module Processor_Interface (
);

  wire _0_IPC, ADRCTL, and_1_out, CLOCK, D_HRH, D_HRL, D_IDL, H_PROM, IPC_ALT, IPC_IPC, IPC_Sel, IPCCNTRL,
       ITRCTL, LDRAM, not_1_out, not_2_out, not_3_out, or_1_out, or_2_out, PROM_AROM_Disable, PROMCNTRL;
  wire [7:0] adder_1_out, controlled_buffer_1_out, controlled_buffer_3_out, controlled_buffer_4_out,
       controlled_buffer_5_out, controlled_buffer_5_out_2, controlled_buffer_6_out, infrastructure_1_out,
       ipc_1_out_3, multiplexer_1_out, multiplexer_2_out, or_3_out, ram_1_data, register_2_q, register_3_q,
       register_3_q_2, register_7_q, register_8_q, rom_1_data;
  wire [15:0] controlled_buffer_2_out, register_1_q, register_6_q, rom_4_data;
  wire [15:8] register_2_q_2;
  wire [31:0] register_4_q, register_5_q, rom_2_data, rom_3_data;

  Register #(.width(16)) register_1 (
    .D({controlled_buffer_5_out, ram_1_data}), .Q(register_1_q), .clk(and_1_out));  // open: en, clr
  and and_1 (and_1_out, not_1_out, not_2_out);
  not not_1 (not_1_out, PROM_AROM_Disable);
  Multiplexer #(.width(8), .enable("false")) multiplexer_1 (
    .in0(register_1_q[7:0]), .in1(register_1_q[15:8]), .out(multiplexer_1_out), .sel(ADRCTL));
  Pull_Resistor pull_resistor_1 (.node(ADRCTL));
  not not_2 (not_2_out, CLOCK);
  IPC ipc_1 (
    .in_1(controlled_buffer_5_out), .in_2({IPC_IPC, IPC_Sel, IPC_ALT, _0_IPC, CLOCK, IPCCNTRL}),
    .out_3(ipc_1_out_3));
  ROM rom_1 (.addr(multiplexer_1_out), .data(rom_1_data));  // open: sel
  Adder adder_1 (.a(ipc_1_out_3), .b(register_2_q), .out(adder_1_out));  // open: cin, cout
  Register #(.width(16)) register_2 (
    .D({adder_1_out, rom_1_data}), .Q({register_2_q_2, register_2_q}), .clk(CLOCK));  // open: en, clr
  Pull_Resistor pull_resistor_2 (.node(adder_1_out));
  assign controlled_buffer_1_out = LDRAM ? register_3_q_2 : 8'bz;  // Controlled_Buffer controlled_buffer_1
  Multiplexer #(.width(8), .enable("false")) multiplexer_2 (
    .in0(register_2_q), .in1(register_2_q_2), .out(multiplexer_2_out), .sel(ITRCTL));
  Pull_Resistor pull_resistor_3 (.node(ITRCTL));
  Register #(.width(16)) register_3 (
    .D(controlled_buffer_2_out), .Q({register_3_q_2, register_3_q}), .clk(CLOCK));  // open: en, clr
  Pull_Resistor pull_resistor_4 (.node(PROMCNTRL));
  assign controlled_buffer_2_out = PROMCNTRL ? {controlled_buffer_5_out_2, controlled_buffer_5_out} : 16'bz;  // Controlled_Buffer controlled_buffer_2
  RAM #(.addrWidth(16), .bus("separate")) ram_1 (
    .addr({register_3_q_2, register_3_q}), .din(controlled_buffer_1_out), .data(ram_1_data), .str(LDRAM));  // open: sel, clk, ld, clr
  ROM #(.dataWidth(32)) rom_2 (.addr(multiplexer_2_out), .data(rom_2_data));  // open: sel
  ROM #(.dataWidth(32)) rom_3 (.addr(multiplexer_2_out), .data(rom_3_data));  // open: sel
  ROM #(.dataWidth(16)) rom_4 (.addr(multiplexer_2_out), .data(rom_4_data));  // open: sel
  Register #(.width(32)) register_4 (.D(rom_2_data), .Q(register_4_q), .clk(not_3_out));  // open: en, clr
  Register #(.width(32)) register_5 (
    .D(rom_3_data),
    .Q({register_5_q[31:25], _0_IPC, IPC_IPC, IPCCNTRL, IPC_Sel, PROMCNTRL, register_5_q[19:0]}),
    .clk(not_3_out));  // open: en, clr
  Register #(.width(16)) register_6 (
    .D(rom_4_data),
    .Q({{5{register_6_q[15]}}, H_PROM, D_HRH, D_HRL, IPC_ALT, D_IDL, ADRCTL, ITRCTL, PROM_AROM_Disable, LDRAM, register_6_q[1:0]}),
    .clk(not_3_out));  // open: en, clr
  not not_3 (not_3_out, CLOCK);
  Register register_7 (.D(controlled_buffer_3_out), .Q(register_7_q), .clk(or_1_out));  // open: en, clr
  assign controlled_buffer_3_out = D_HRH ? ram_1_data : 8'bz;  // Controlled_Buffer controlled_buffer_3
  or or_1 (or_1_out, D_HRH, 1'b0);
  assign controlled_buffer_4_out = D_HRL ? ram_1_data : 8'bz;  // Controlled_Buffer controlled_buffer_4
  Register register_8 (.D(controlled_buffer_4_out), .Q(register_8_q), .clk(or_2_out));  // open: en, clr
  or or_2 (or_2_out, D_HRL, 1'b0);
  assign {controlled_buffer_5_out_2, controlled_buffer_5_out} = H_PROM ? {register_7_q, register_8_q} : 16'bz;  // Controlled_Buffer controlled_buffer_5
  Pull_Resistor pull_resistor_5 (.node(H_PROM));
  Clock clock_1 (.out(CLOCK));
  assign controlled_buffer_6_out = D_IDL ? ram_1_data : 8'bz;  // Controlled_Buffer controlled_buffer_6
  assign or_3_out = controlled_buffer_6_out | {register_6_q[0], register_5_q[31:25]};  // OR_Gate or_3, 8 bits wide
  Pull_Resistor pull_resistor_6 (.node(controlled_buffer_6_out));
  Pull_Resistor pull_resistor_7 (.node({controlled_buffer_5_out_2, controlled_buffer_5_out}));
  Infrastructure infrastructure_1 (
    .Clock(CLOCK), .C_IN(register_6_q[1]), .Control_Lines(register_4_q), .ABH(controlled_buffer_5_out_2),
    .ABL(controlled_buffer_5_out), .Input_Data_Latch(or_3_out), .OUT(infrastructure_1_out),
    .Control_Lines_2_0(register_5_q[19:0]), .IR5(register_3_q[5]));
  Hex_Digit_Display hex_digit_display_1 (.value(infrastructure_1_out[3:0]));  // open: dp
  Hex_Digit_Display hex_digit_display_2 (.value(infrastructure_1_out[7:4]));  // open: dp
  // also tied to GND on the sheet: register_6_q[15]

  // Notes on the sheet:
  //   Addressing ROM
  //   contents of rom_1 (hex, n*v repeats v):
  //   16*0 1 7*0 a 23*0 e 7*0 18 84*0 2b 27*0 28 70*0 1e
  //   Program RAM
  //   Instruction Rom
  //   contents of rom_2 (hex, n*v repeats v):
  //   0 101400 e00 0 80000000 0 1400 0 80000000 0 200000 0 0 0 131400 e00 e00 0 80000000 0 1400 0 80000000
  //   0 200000 5*0 131400 e00 e00 0 80000000 0 1400 0 80000000 0 0 42000002
  //   contents of rom_3 (hex, n*v repeats v):
  //   0 2c82000 c00008 c00100 600900 d00c60 c01020 c00100 c00100 1100c60 c01000 c00006 c00000 1100c66
  //   2c82000 2c01000 c00008 c00100 600900 d00c60 c01020 c00100 c00100 1100c60 2c01000 c00006 c00000
  //   1100c66 c00000 c00000 2c22000 2c01000 c00008 c00100 600900 d00c60 c01020 c00100 c00100 1100c60
  //   d00c66 c01000 1100c66 d00c66 d04400 d00c66 d02800
  //   contents of rom_4 (hex, n*v repeats v):
  //   0 10 18 18 ff98 18 58 18 18 10 10 18 18 10 10 18 18 18 ff98 18 58 18 18 10 10 18 18 4*10 18 18 18
  //   ff98 18 58 18 18 10 18 58 10 18 58 18 58
  //   This area
  //   Note: This area is a future addition and is not yet finished
endmodule

module PC_Inc (
  input  [7:0] PCL,
  input  [7:0] PCH,
  output [7:0] PCL_2,
  output [7:0] PCH_2
);

  Adder #(.width(16)) adder_1 (.a({PCH, PCL}), .b(16'h1), .out({PCH_2, PCL_2}), .cin(1'b0));  // open: cout
endmodule

module StatusRegister (
  input  [14:0] Control,
  input  [7:0] DB_In,
  input  IR5,
  input  COUT,
  input  AVR,
  output [7:0] DB_Out
);

  wire and_1_out, and_2_out, and_3_out, and_4_out, buffer_1_out, buffer_2_out, buffer_3_out, buffer_4_out,
       controlled_buffer_1_out, controlled_buffer_4_out, controlled_buffer_6_out, controlled_buffer_10_out,
       nor_1_out, or_2_out, or_3_out, or_4_out, register_1_q, register_2_q, register_3_q, register_4_q,
       VCNTRL;
  wire [7:0] pull_resistor_1_node;

  nor nor_1 (nor_1_out, DB_In[7], DB_In[6], DB_In[5], DB_In[4], DB_In[3], DB_In[2], DB_In[1], DB_In[0]);
  or or_1 (VCNTRL, Control[6], Control[7], Control[8], Control[9]);
  assign controlled_buffer_1_out = Control[1] ? DB_In[0] : 1'bz;  // Controlled_Buffer controlled_buffer_1
  assign controlled_buffer_1_out = Control[2] ? IR5 : 1'bz;  // Controlled_Buffer controlled_buffer_2
  assign controlled_buffer_1_out = Control[3] ? COUT : 1'bz;  // Controlled_Buffer controlled_buffer_3
  assign controlled_buffer_4_out = Control[4] ? DB_In[1] : 1'bz;  // Controlled_Buffer controlled_buffer_4
  assign controlled_buffer_4_out = Control[5] ? nor_1_out : 1'bz;  // Controlled_Buffer controlled_buffer_5
  assign controlled_buffer_6_out = Control[6] ? DB_In[6] : 1'bz;  // Controlled_Buffer controlled_buffer_6
  assign controlled_buffer_6_out = Control[7] ? AVR : 1'bz;  // Controlled_Buffer controlled_buffer_7
  assign controlled_buffer_6_out = Control[8] ? 1'b1 : 1'bz;  // Controlled_Buffer controlled_buffer_8
  assign controlled_buffer_6_out = Control[9] ? 1'b0 : 1'bz;  // Controlled_Buffer controlled_buffer_9
  assign controlled_buffer_10_out = Control[10] ? DB_In[7] : 1'bz;  // Controlled_Buffer controlled_buffer_10
  or or_2 (or_2_out, Control[4], Control[5]);
  or or_3 (or_3_out, Control[1], Control[3], Control[2]);
  buf buffer_1 (buffer_1_out, or_2_out);
  Register #(.width(1)) register_1 (
    .D(controlled_buffer_1_out), .Q(register_1_q), .clk(buffer_2_out));  // open: en, clr
  buf buffer_2 (buffer_2_out, or_4_out);
  or or_4 (or_4_out, 1'b0, or_3_out);
  Register #(.width(1)) register_2 (
    .D(controlled_buffer_4_out), .Q(register_2_q), .clk(buffer_1_out));  // open: en, clr
  Register #(.width(1)) register_3 (
    .D(controlled_buffer_6_out), .Q(register_3_q), .clk(buffer_3_out));  // open: en, clr
  buf buffer_3 (buffer_3_out, VCNTRL);
  Register #(.width(1)) register_4 (
    .D(controlled_buffer_10_out), .Q(register_4_q), .clk(buffer_4_out));  // open: en, clr
  buf buffer_4 (buffer_4_out, Control[10]);
  and and_1 (and_1_out, Control[11], register_1_q);
  and and_2 (and_2_out, Control[12], register_2_q);
  and and_3 (and_3_out, Control[13], register_3_q);
  and and_4 (and_4_out, Control[14], register_4_q);
  assign DB_Out = Control[0] ? pull_resistor_1_node : 8'bz;  // Controlled_Buffer controlled_buffer_11
  Pull_Resistor pull_resistor_1 (.node(pull_resistor_1_node));
  or or_5 (pull_resistor_1_node[0], and_1_out, and_2_out, and_3_out, and_4_out);

  // Other names for the same wires on the sheet: P_DB = Control[0]; DB0_C = Control[1]; IR5_C = Control[2];
  //   ACR_C = Control[3]; DBI_Z = Control[4]; DBZ_Z = Control[5]; DB6_V = Control[6]; AVR_V = Control[7];
  //   _1_V = Control[8]; _0_V = Control[9]; DB7_N = Control[10]; C_DB = Control[11]; Z_DB = Control[12];
  //   V_DB = Control[13]; N_DB = Control[14]
endmodule

module INST_PC_Formula (
  input  [7:0] INST_PC_IN,
  input  [7:0] PC_IN,
  output [7:0] OUT
);

  wire [7:0] adder_1_out, adder_2_out, divider_1_rem, divider_2_rem, multiplier_1_out, multiplier_2_out,
       subtractor_1_out, subtractor_2_out;

  Divider divider_1 (.a(PC_IN), .b(8'h2), .rem(divider_1_rem));  // open: out, upper
  Subtractor subtractor_1 (.a(8'h1), .b(divider_1_rem), .out(subtractor_1_out));  // open: bin, bout
  Multiplier multiplier_1 (.a(subtractor_1_out), .b(8'h2), .out(multiplier_1_out));  // open: cin, cout
  Divider divider_2 (.a(PC_IN), .b(8'h2), .rem(divider_2_rem));  // open: out, upper
  Adder adder_1 (.a(multiplier_1_out), .b(divider_2_rem), .out(adder_1_out));  // open: cin, cout
  Subtractor subtractor_2 (.a(adder_1_out), .b(8'h1), .out(subtractor_2_out));  // open: bin, bout
  Multiplier multiplier_2 (.a(subtractor_2_out), .b(8'h2), .out(multiplier_2_out));  // open: cin, cout
  Adder adder_2 (.a(adder_1_out), .b(multiplier_2_out), .out(adder_2_out));  // open: cin, cout
  Adder adder_3 (.a(INST_PC_IN), .b(adder_2_out), .out(OUT));  // open: cin, cout
endmodule

module IPC (
  input  [7:0] in_1,
  input  [5:0] in_2,
  output [7:0] out_3
);

  wire [7:0] adder_1_out, controlled_buffer_1_out, inst_pc_formula_1_out, Instruction_PC_q, multiplexer_1_out;

  Multiplexer #(.width(8)) multiplexer_1 (.in0(8'h1), .in1(in_1), .out(multiplexer_1_out), .sel(in_2[4]));  // open: en
  INST_PC_Formula inst_pc_formula_1 (
    .PC_IN(multiplexer_1_out), .OUT(inst_pc_formula_1_out), .INST_PC_IN(Instruction_PC_q));
  assign controlled_buffer_1_out = in_2[3] ? inst_pc_formula_1_out : 8'bz;  // Controlled_Buffer controlled_buffer_1
  assign controlled_buffer_1_out = in_2[5] ? adder_1_out : 8'bz;  // Controlled_Buffer controlled_buffer_2
  assign controlled_buffer_1_out = in_2[2] ? {8{1'b0}} : 8'bz;  // Controlled_Buffer controlled_buffer_3
  Adder adder_1 (.a(Instruction_PC_q), .b(multiplexer_1_out), .out(adder_1_out));  // open: cin, cout
  Register Instruction_PC (.D(controlled_buffer_1_out), .Q(Instruction_PC_q), .clk(in_2[1]));  // open: en, clr
  assign out_3 = in_2[0] ? Instruction_PC_q : 8'bz;  // Controlled_Buffer controlled_buffer_4

  // Other names for the same wires on the sheet: IPCCNTRL = in_2[0]; CLOCK = in_2[1]; _0_IPC = in_2[2];
  //   IPC_ALT = in_2[3]; IPC_Sel = in_2[4]; IPC_IPC = in_2[5]
endmodule

module PC (
  input  [7:0] SB_In,
  input  [7:0] ADH_in,
  input  [7:0] ADL_in,
  input  [8:0] in_4,
  output [7:0] ADL_Out,
  output [7:0] ADH_Out,
  output [7:0] DB_Out
);

  wire buffer_1_out, or_1_out;
  wire [7:0] controlled_buffer_1_out, controlled_buffer_3_out, pc_inc_1_pch_2, pc_inc_1_pcl_2;
  wire [15:0] PC_q;

  assign controlled_buffer_1_out = in_4[3] ? pc_inc_1_pch_2 : 8'bz;  // Controlled_Buffer controlled_buffer_1
  assign controlled_buffer_1_out = in_4[1] ? ADH_in : 8'bz;  // Controlled_Buffer controlled_buffer_2
  PC_Inc pc_inc_1 (.PCL(PC_q[7:0]), .PCH(PC_q[15:8]), .PCL_2(pc_inc_1_pcl_2), .PCH_2(pc_inc_1_pch_2));
  assign controlled_buffer_3_out = in_4[2] ? pc_inc_1_pcl_2 : 8'bz;  // Controlled_Buffer controlled_buffer_3
  assign controlled_buffer_3_out = in_4[8] ? SB_In : 8'bz;  // Controlled_Buffer controlled_buffer_4
  assign controlled_buffer_3_out = in_4[0] ? ADL_in : 8'bz;  // Controlled_Buffer controlled_buffer_5
  Register #(.width(16)) PC (
    .D({controlled_buffer_1_out, controlled_buffer_3_out}), .Q(PC_q), .clk(buffer_1_out));  // open: en, clr
  Pull_Resistor pull_resistor_1 (.node({controlled_buffer_1_out, controlled_buffer_3_out}));
  buf buffer_1 (buffer_1_out, or_1_out);
  or or_1 (or_1_out, in_4[2], in_4[8], in_4[0], in_4[3], in_4[1]);
  assign ADL_Out = in_4[6] ? PC_q[7:0] : 8'bz;  // Controlled_Buffer controlled_buffer_6
  assign DB_Out = in_4[4] ? PC_q[7:0] : 8'bz;  // Controlled_Buffer controlled_buffer_7
  assign ADH_Out = in_4[7] ? PC_q[15:8] : 8'bz;  // Controlled_Buffer controlled_buffer_8
  assign DB_Out = in_4[5] ? PC_q[15:8] : 8'bz;  // Controlled_Buffer controlled_buffer_9

  // Other names for the same wires on the sheet: ADL_PC = in_4[0]; ADH_PC = in_4[1]; PCL_PCL = in_4[2];
  //   PCH_PCH = in_4[3]; PCL_DB = in_4[4]; PCH_DB = in_4[5]; PCL_ADL = in_4[6]; PCH_ADH = in_4[7]; SB_PCL = in_4[8]

  // Notes on the sheet:
  //   Note: register should be implemented as two 8 bit registers
endmodule
